// Logisim project Z23.circ as structural Verilog: 5 circuits, main circuit Z23
module Z23 (
);

  Memory memory_1 ();  // open: imput, load, adress, clock, out_5
  RegisterFile registerfile_1 ();  // open: data, rs, rd, rw, R_rs, R_rd, clk
  InstructionMemory instructionmemory_1 ();  // open: Clock, Reset, Current_Instruction
  ALU alu_1 ();  // open: A, B, sel, Out
endmodule

module Memory (
  input  [7:0] imput,
  input  load,
  input  [5:0] adress,
  input  clock,
  output [7:0] out_5
);

  wire not_1_out;

  assign out_5 = load ? imput : 8'bz;  // Controlled_Buffer controlled_buffer_1
  not not_1 (not_1_out, load);
  RAM #(.addrWidth(6)) ram_1 (.addr(adress), .data(out_5), .clk(clock), .ld(not_1_out));  // open: sel, clr
endmodule

module InstructionMemory (
  input  Clock,
  input  Reset,
  output [15:0] Current_Instruction
);

  wire [5:0] adder_1_out, register_1_q;

  Adder #(.width(6)) adder_1 (.a(register_1_q), .b(6'b000001), .out(adder_1_out));  // open: cin, cout
  Register #(.width(6)) register_1 (.D(adder_1_out), .Q(register_1_q), .clk(Clock), .clr(Reset));  // open: en
  RAM #(.addrWidth(6), .dataWidth(16), .Datafile_on_reset("C:\\Users\\sebto\\Dropbox\\Sebastián\\Estudios\\Tecnología de computadores\\Topic 3\\Memory")) ram_1 (
    .addr(register_1_q), .data(Current_Instruction));  // open: sel, clk, ld, clr
endmodule

module RegisterFile (
  input  [7:0] data,
  input  rs,
  input  rd,
  input  rw,
  input  clk,
  output [7:0] R_rs,
  output [7:0] R_rd
);

  wire and_1_out, and_2_out;
  wire [7:0] r0_q, r1_q;

  and and_1 (and_1_out, ~rd, rw);  // AND_Gate
  and and_2 (and_2_out, rd, rw);
  Register r0 (.D(data), .en(and_1_out), .Q(r0_q), .clk(clk));  // open: clr
  Register r1 (.D(data), .en(and_2_out), .Q(r1_q), .clk(clk));  // open: clr
  Multiplexer #(.width(8), .enable("false")) multiplexer_1 (.in0(r0_q), .in1(r1_q), .out(R_rs), .sel(rs));
  Multiplexer #(.width(8), .enable("false")) multiplexer_2 (.in0(r0_q), .in1(r1_q), .out(R_rd), .sel(rd));
endmodule

module ALU (
  input  [7:0] A,
  input  [7:0] B,
  input  [2:0] sel,
  output [7:0] Out
);

  wire [7:0] addr_1_out_3, comp_1_out_3, div_1_out, mod_1_out, mult_1_out, sub_1_out_3;

  addr addr_1 (.A(A), .B(B), .out_3(addr_1_out_3));
  sub sub_1 (.A(A), .B(B), .out_3(sub_1_out_3));
  mult mult_1 (.A(A), .B(B), .Out(mult_1_out));
  div div_1 (.A(A), .B(B), .Out(div_1_out));
  mod mod_1 (.A(A), .B(B), .out(mod_1_out));
  comp comp_1 (.A(A), .B(B), .out_3(comp_1_out_3));
  Multiplexer #(.select(3), .width(8)) multiplexer_1 (
    .in0(A), .in1(B), .in2(addr_1_out_3), .in3(sub_1_out_3), .in4(mult_1_out), .in5(div_1_out),
    .in6(mod_1_out), .in7(comp_1_out_3), .out(Out), .sel(sel));  // open: en
endmodule
